# Fritzing sketch Projeto PCB - 2 (saved by Fritzing 0.9.3b)
breadboards: 1

parts:
  U1 = Voltage Regulator - Variable [package="TO220 [THT]"]
  J4 = screw terminal, 3 pins
  J5 = screw terminal, 4 pins
  Q3 = PNP-Transistor [package="TO92 [THT]"]
  Q4 = PNP-Transistor [package="TO92 [THT]"]
  Q5 = PNP-Transistor [package="TO92 [THT]"]
  R7 = Resistor [tolerance=±5% resistance=100 package=THT]
  R8 = Resistor [tolerance=±5% resistance=4.7k package=THT]
  R9 = Resistor [tolerance=±5% resistance=1M package=THT]
  R1 = Resistor [tolerance=±5% resistance=1k package=THT]
  R3 = Resistor [tolerance=±5% resistance=1k package=THT]
  R2 = Resistor [tolerance=±5% resistance=1k package=THT]
  J2 = screw terminal, 3 pins
  J1 = screw terminal, 2 pins
  U2 = Voltage Regulator - 5V [package="TO220 [THT]"]
  part = Arduino Nano (Rev3.0)

nets:
  GND: U1.ADJ, J1.pin1, U2.GND, part.VIN
  N1: U1.OUT, J4.pin2, Q3.B, Q4.B, Q5.B, J2.pin2, J1.pin2, part.GND
  N2: U1.IN, J5.pin1, U2.input_voltage
  N3: J4.pin1, R8.Pin_0, part.A0
  N4: J4.pin3, R7.Pin_0
  N5: J5.pin2, Q3.E
  N6: J5.pin3, Q4.E
  N7: J5.pin4, Q5.E
  N8: Q3.C, R2.Pin_0
  N9: Q4.C, R3.Pin_0
  N10: Q5.C, R1.Pin_0
  N11: R7.Pin_1, R8.Pin_1, R9.Pin_1, part.5V
  N12: R9.Pin_0, J2.pin3, part.D6
  N13: R1.Pin_1, part.D5
  N14: R3.Pin_1, part.D4
  N15: R2.Pin_1, part.D3
  N16: J2.pin1, U2.output_voltage

notes:
  12v R
  19v
  LED
  RGB
  IR
  MOTOR
  12V/PWM
  12v P
