# Fritzing sketch Projeto PCB (saved by Fritzing 0.9.3b)
breadboards: 1

parts:
  Componente1 = Arduino Nano (Rev3.0)
  J1 = Screw terminal - 2 pins [package=THT]
  Q1 = PHOTOTRANSISTOR REFLECTIVE OBJECT SENSOR [package=qrb1114-side]  # not connected
  U1 = Voltage Regulator - Variable [package="TO220 [THT]"]
  U2 = Voltage Regulator - 5V [package="TO220 [THT]"]
  J2 = Screw terminal - 2 pins [package=THT]
  J3 = Screw terminal - 2 pins [package=THT]

nets:
  N1: Componente1.GND, J1.pin2, U1.OUT, J2.pin2, J3.pin1
  VIN: Componente1.VIN, J1.pin1, U1.ADJ, U2.GND
  N2: U1.IN, U2.input_voltage, J3.pin2
  N3: U2.output_voltage, J2.pin1
